# Fritzing sketch HardwareArchitecture (saved by Fritzing 1.0.7)

parts:
  Raspberry_Pi_AI_HAT+_Hailo-8_26_TOPS = Raspberry Pi 5
  Load_Cell1 = Load Cell - Red/white/black/green
  LCD1 = DIYables LCD 2004 I2C (20x4, Blue Backlight) [part_number=DIYables-LCD2004-I2C-Blue mn=sd]
  CONFIRM_/_SAVE = Round Pushbutton
  U1 = mystery part, 3 pins [chip_label=GND]
  U2 = mystery part, 3 pins [chip_label=DT]
  U3 = mystery part, 3 pins [chip_label=SCK]
  U4 = mystery part, 3 pins [chip_label=VCC]
  U5 = mystery part, 3 pins [chip_label=E+]
  U6 = mystery part, 3 pins [chip_label=E-]
  U7 = mystery part, 3 pins [chip_label=A-]
  U8 = mystery part, 3 pins [chip_label=A+]
  U9 = mystery part, 3 pins [chip_label=B-]  # not connected
  U10 = mystery part, 3 pins [chip_label=B+]  # not connected
  NEXT_/_CHANGE = Round Pushbutton
  TARE = Round Pushbutton
  Part1 = Adafruit 4-channel I2C-safe Bi-directional Logic Level Converter [part_number="Adafruit #757"]
  Start = Round Pushbutton

nets:
  N1: Raspberry_Pi_AI_HAT+_Hailo-8_26_TOPS.3V3, U4.pin2, Part1.LV
  5V: Raspberry_Pi_AI_HAT+_Hailo-8_26_TOPS.5V, Raspberry_Pi_AI_HAT+_Hailo-8_26_TOPS.Fan-5V, LCD1.VCC, Part1.HV
  N2: Raspberry_Pi_AI_HAT+_Hailo-8_26_TOPS.GPIO2, Part1.A1
  N3: Raspberry_Pi_AI_HAT+_Hailo-8_26_TOPS.GPIO3, Part1.A2
  GND: Raspberry_Pi_AI_HAT+_Hailo-8_26_TOPS.GND, Raspberry_Pi_AI_HAT+_Hailo-8_26_TOPS.Fan-GND, LCD1.GND, CONFIRM_/_SAVE.leg1, U1.pin2, NEXT_/_CHANGE.leg1, TARE.leg1, Part1.GND, Start.leg1
  N4: Raspberry_Pi_AI_HAT+_Hailo-8_26_TOPS.GPIO17, Start.leg0
  N5: Raspberry_Pi_AI_HAT+_Hailo-8_26_TOPS.GPIO27, TARE.leg0
  N6: Raspberry_Pi_AI_HAT+_Hailo-8_26_TOPS.GPIO22, NEXT_/_CHANGE.leg0
  N7: Raspberry_Pi_AI_HAT+_Hailo-8_26_TOPS.GPIO23, CONFIRM_/_SAVE.leg0
  N8: Raspberry_Pi_AI_HAT+_Hailo-8_26_TOPS.GPIO5, U2.pin2
  N9: Raspberry_Pi_AI_HAT+_Hailo-8_26_TOPS.GPIO6, U3.pin2
  N10: Load_Cell1.wire1, U5.pin2
  N11: Load_Cell1.wire2, U7.pin2
  N12: Load_Cell1.wire3, U6.pin2
  N13: Load_Cell1.wire4, U8.pin2
  N14: LCD1.SDA, Part1.B1
  N15: LCD1.SCL, Part1.B2

notes:
  CAM
  Load Cell
  HX711
  Raspberry Pi 5
  Level Shifters
  LCD
  CONFIRM / SAVE
  NEXT / CHANGE
  TARE
  Start

custom parts:
  Raspberry Pi 5: The RPi5, a faster version of the awesome Raspberry Pi4B ARM Board with 40 pin gpio.
  Load Cell - Red/white/black/green: A rectangle load cell/weighting pressure Sensor with four wires - Red, white, black, green. Normally corresponding with E+, E-, A+, A- respectively.
  DIYables LCD 2004 I2C (20x4, Blue Backlight): DIYables LCD 2004 I2C (20x4, Blue Backlight) - 20x4 character LCD with blue backlight and an I2C interface (PCF8574 I/O expander, contrast potentiometer). 4-pin header: GND, VCC, SDA, SCL. Fits most LCD 2004 I2C modules.
